// Logisim project ALU.circ as structural Verilog: 2 circuits, main circuit main
module main (
  input  f,
  input  zx,
  input  nx,
  input  no,
  input  x0,
  input  x1,
  input  x2,
  input  x3,
  input  zy,
  input  ny,
  input  y0,
  input  y1,
  input  y2,
  input  y3,
  output out_15,
  output out_16,
  output out_17,
  output out_18
);

  wire adder_1_cout, adder_2_cout, adder_3_cout, and_1_out, and_2_out, and_3_out, and_4_out, and_5_out,
       and_6_out, and_7_out, and_8_out, fmux_1_out_5, fmux_2_out_5, fmux_3_out_5, fmux_4_out_5, not_1_out,
       not_2_out, not_3_out, xor_1_out, xor_2_out, xor_3_out, xor_4_out, xor_5_out, xor_6_out, xor_7_out,
       xor_8_out;

  not not_1 (not_1_out, zx);
  not not_2 (not_2_out, zy);
  and and_1 (and_1_out, x0, not_1_out);
  and and_2 (and_2_out, x1, not_1_out);
  and and_3 (and_3_out, x2, not_1_out);
  and and_4 (and_4_out, x3, not_1_out);
  and and_5 (and_5_out, y0, not_2_out);
  and and_6 (and_6_out, y1, not_2_out);
  and and_7 (and_7_out, y2, not_2_out);
  and and_8 (and_8_out, y3, not_2_out);
  xor xor_1 (xor_1_out, and_1_out, nx);
  xor xor_2 (xor_2_out, and_2_out, nx);
  xor xor_3 (xor_3_out, and_3_out, nx);
  xor xor_4 (xor_4_out, and_4_out, nx);
  xor xor_5 (xor_5_out, and_5_out, ny);
  xor xor_6 (xor_6_out, and_6_out, ny);
  xor xor_7 (xor_7_out, and_7_out, ny);
  xor xor_8 (xor_8_out, and_8_out, ny);
  not not_3 (not_3_out, 1'b1);
  fmux fmux_1 (.f(f), .cout(not_3_out), .x(xor_1_out), .y(xor_5_out), .out_5(fmux_1_out_5));
  Adder #(.width(1)) adder_1 (.a(xor_5_out), .b(xor_1_out), .cin(not_3_out), .cout(adder_1_cout));  // open: out
  fmux fmux_2 (.f(f), .cout(adder_1_cout), .x(xor_2_out), .y(xor_6_out), .out_5(fmux_2_out_5));
  Adder #(.width(1)) adder_2 (.a(xor_2_out), .b(xor_6_out), .cin(adder_1_cout), .cout(adder_2_cout));  // open: out
  fmux fmux_3 (.f(f), .cout(adder_2_cout), .x(xor_3_out), .y(xor_7_out), .out_5(fmux_3_out_5));
  Adder #(.width(1)) adder_3 (.a(xor_7_out), .b(xor_3_out), .cin(adder_2_cout), .cout(adder_3_cout));  // open: out
  fmux fmux_4 (.f(f), .cout(adder_3_cout), .x(xor_4_out), .y(xor_8_out), .out_5(fmux_4_out_5));
  xor xor_9 (out_15, fmux_1_out_5, no);
  xor xor_10 (out_16, fmux_2_out_5, no);
  xor xor_11 (out_17, fmux_3_out_5, no);
  xor xor_12 (out_18, fmux_4_out_5, no);
endmodule

module fmux (
  input  f,
  input  cout,
  input  x,
  input  y,
  output out_5
);

  wire and_1_out, and_2_out, and_3_out, and_4_out, and_5_out, not_1_out, not_2_out, not_3_out, not_4_out;

  not not_1 (not_1_out, f);
  not not_2 (not_2_out, x);
  not not_3 (not_3_out, cout);
  not not_4 (not_4_out, y);
  and and_1 (and_1_out, f, cout, not_2_out, not_4_out);
  and and_2 (and_2_out, f, cout, x, y);
  and and_3 (and_3_out, f, not_3_out, x, not_4_out);
  and and_4 (and_4_out, f, not_3_out, not_2_out, y);
  and and_5 (and_5_out, not_1_out, x, y);
  or or_1 (out_5, and_1_out, and_2_out, and_3_out, and_4_out, and_5_out);
endmodule
