// Logisim project hw1.circ as structural Verilog: 3 circuits, main circuit q3
module q3 (
  input  A,
  input  B,
  input  C,
  input  D,
  output out_5
);

  wire and_1_out, and_2_out, and_3_out, and_4_out, and_5_out, and_6_out, and_7_out, and_8_out, not_1_out,
       not_2_out, not_3_out, not_4_out;

  not not_1 (not_1_out, A);
  not not_2 (not_2_out, B);
  not not_3 (not_3_out, C);
  not not_4 (not_4_out, D);
  and and_1 (and_1_out, not_1_out, not_2_out, not_3_out, D);
  and and_2 (and_2_out, not_1_out, not_2_out, C, not_4_out);
  and and_3 (and_3_out, not_1_out, B, not_3_out, not_4_out);
  and and_4 (and_4_out, not_1_out, B, C, D);
  and and_5 (and_5_out, A, B, not_3_out, D);
  and and_6 (and_6_out, A, not_2_out, not_3_out, not_4_out);
  and and_7 (and_7_out, A, B, C, not_4_out);
  and and_8 (and_8_out, A, not_2_out, C, D);
  or or_1 (out_5, and_8_out, and_3_out, and_1_out, and_2_out, and_4_out, and_5_out, and_6_out, and_7_out);
endmodule

module q1 (
  input  c1,
  input  c0,
  output D11,
  output D01,
  output D10,
  output D00
);

  wire not_1_out, not_2_out;

  not not_1 (not_1_out, c1);
  not not_2 (not_2_out, c0);
  and and_1 (D11, c1, c0);
  and and_2 (D01, not_1_out, c0);
  and and_3 (D10, c1, not_2_out);
  and and_4 (D00, not_1_out, not_2_out);
endmodule

module q2 (
  input  x2,
  input  x1,
  input  x0,
  input  y2,
  input  y1,
  input  y0,
  output out_7
);

  wire and_1_out, and_2_out, not_1_out, not_2_out, or_1_out;

  not not_1 (not_1_out, x0);
  not not_2 (not_2_out, y0);
  and and_1 (and_1_out, x0, not_2_out);
  and and_2 (and_2_out, not_1_out, y0);
  or or_1 (or_1_out, and_1_out, and_2_out);
  not not_3 (out_7, or_1_out);
endmodule
