// Logisim project lab2.circ as structural Verilog: 3 circuits, main circuit 4bit-neg
module _4bit_neg (
  input  a0,
  input  a1,
  input  a2,
  input  a3,
  output out_5,
  output out_6,
  output out_7,
  output out_8
);

  wire adder_1_cout, adder_2_cout, adder_3_cout, not_1_out, not_2_out, not_3_out, not_4_out, not_5_out,
       not_6_out, not_7_out;

  not not_1 (not_1_out, a0);
  not not_2 (not_2_out, 1'b1);
  not not_3 (not_3_out, a1);
  not not_4 (not_4_out, 1'b1);
  not not_5 (not_5_out, a2);
  not not_6 (not_6_out, a3);
  not not_7 (not_7_out, 1'b1);
  Adder #(.width(1)) adder_1 (.a(1'b1), .b(not_1_out), .out(out_5), .cout(adder_1_cout));  // open: cin
  Adder #(.width(1)) adder_2 (.a(not_2_out), .b(not_3_out), .out(out_6), .cin(adder_1_cout), .cout(adder_2_cout));
  Adder #(.width(1)) adder_3 (.a(not_4_out), .b(not_5_out), .out(out_7), .cin(adder_2_cout), .cout(adder_3_cout));
  Adder #(.width(1)) adder_4 (.a(not_6_out), .b(not_7_out), .out(out_8), .cin(adder_3_cout));  // open: cout
endmodule

module subtractor (
  input  a0,
  input  b0,
  input  a1,
  input  b1,
  input  a2,
  input  b2,
  input  a3,
  input  b3,
  output out_9,
  output out_10,
  output out_11,
  output out_12
);

  wire adder_1_cout, adder_2_cout, adder_3_cout, n4bit_neg_1_out_5, n4bit_neg_1_out_6, n4bit_neg_1_out_7,
       n4bit_neg_1_out_8;

  _4bit_neg u_4bit_neg_1 (
    .a0(b0), .a1(b1), .a2(b2), .a3(b3), .out_5(n4bit_neg_1_out_5), .out_6(n4bit_neg_1_out_6),
    .out_7(n4bit_neg_1_out_7), .out_8(n4bit_neg_1_out_8));
  Adder #(.width(1)) adder_1 (.a(a0), .b(n4bit_neg_1_out_5), .out(out_9), .cout(adder_1_cout));  // open: cin
  Adder #(.width(1)) adder_2 (.a(a1), .b(n4bit_neg_1_out_6), .out(out_10), .cin(adder_1_cout), .cout(adder_2_cout));
  Adder #(.width(1)) adder_3 (.a(a2), .b(n4bit_neg_1_out_7), .out(out_11), .cin(adder_2_cout), .cout(adder_3_cout));
  Adder #(.width(1)) adder_4 (.a(a3), .b(n4bit_neg_1_out_8), .out(out_12), .cin(adder_3_cout));  // open: cout

  // Notes on the sheet:
  //   Authentic work of Jiarong Li
  //   And Zhengyao Gu
endmodule

module comparator (
  input  a3,
  input  b3,
  input  a2,
  input  b2,
  input  a1,
  input  b1,
  input  a0,
  input  b0,
  output out_9
);

  wire adder_1_out, adder_2_out, adder_3_out, adder_4_out, not_1_out, not_2_out, not_3_out, not_4_out;

  Adder #(.width(1)) adder_1 (.a(a3), .b(b3), .out(adder_1_out));  // open: cin, cout
  Adder #(.width(1)) adder_2 (.a(a2), .b(b2), .out(adder_2_out));  // open: cin, cout
  Adder #(.width(1)) adder_3 (.a(a1), .b(b1), .out(adder_3_out));  // open: cin, cout
  Adder #(.width(1)) adder_4 (.a(a0), .b(b0), .out(adder_4_out));  // open: cin, cout
  not not_1 (not_1_out, adder_1_out);
  not not_2 (not_2_out, adder_2_out);
  not not_3 (not_3_out, adder_3_out);
  not not_4 (not_4_out, adder_4_out);
  and and_1 (out_9, not_1_out, not_2_out, not_4_out);

  // Notes on the sheet:
  //   Authentic work of Jiarong Li
  //   And Zhengyao Gu
endmodule
