// Logisim project saturate2.circ as structural Verilog: 4 circuits, main circuit main
module main (
  input  down,
  input  clear
);

  wire clock_1_out, out_1_bot, out_1_lbot, out_1_ltop, out_1_out_6, out_1_rbot, out_1_rtop, out_1_top;
  wire [1:0] next_1_out_5, register_1_q;

  next next_1 (.d(down), .q1(register_1_q[1]), .q0(register_1_q[0]), .out_4(next_1_out_5[1]), .out_5(next_1_out_5[0]));
  Clock clock_1 (.out(clock_1_out));
  Register #(.width(2)) register_1 (.D(next_1_out_5), .en(1'b1), .Q(register_1_q), .clk(clock_1_out), .clr(clear));
  out out_1 (
    .q1(register_1_q[1]), .q0(register_1_q[0]), .top(out_1_top), .ltop(out_1_ltop), .rtop(out_1_rtop),
    .out_6(out_1_out_6), .lbot(out_1_lbot), .rbot(out_1_rbot), .bot(out_1_bot));
  _7_Segment_Display u_7_segment_display_1 (
    .g(out_1_out_6), .f(out_1_ltop), .a(out_1_top), .b(out_1_rtop), .e(out_1_lbot), .d(out_1_bot),
    .c(out_1_rbot));  // open: dp

  // Notes on the sheet:
  //   Zhengyao Gu
  //   Sarah Strand
endmodule

module next (
  input  d,
  input  q1,
  input  q0,
  output out_4,
  output out_5
);

  wire and_1_out, and_2_out, mux_1_out_4, mux_2_out_4, not_1_out, not_2_out, not_3_out, not_4_out, not_5_out,
       not_6_out, or_1_out, xor_1_out, xor_2_out;

  not not_1 (not_1_out, d);
  not not_2 (not_2_out, q1);
  not not_3 (not_3_out, q0);
  and and_1 (and_1_out, d, not_2_out, not_3_out);
  and and_2 (and_2_out, not_1_out, q1, q0);
  xor xor_1 (xor_1_out, q1, q0);
  xor xor_2 (xor_2_out, q1, q0);
  not not_4 (not_4_out, q0);
  not not_5 (not_5_out, xor_1_out);
  not not_6 (not_6_out, q0);
  or or_1 (or_1_out, and_1_out, and_2_out);
  mux mux_1 (.New(not_5_out), .Original(xor_2_out), .sel(d), .out_4(mux_1_out_4));
  mux mux_2 (.New(not_6_out), .Original(not_4_out), .sel(d), .out_4(mux_2_out_4));
  mux mux_3 (.New(q1), .Original(mux_1_out_4), .sel(or_1_out), .out_4(out_4));
  mux mux_4 (.New(q0), .Original(mux_2_out_4), .sel(or_1_out), .out_4(out_5));
endmodule

module out (
  input  q1,
  input  q0,
  output top,
  output ltop,
  output rtop,
  output out_6,
  output lbot,
  output rbot,
  output bot
);

  wire and_2_out, and_3_out, not_1_out, not_2_out, not_3_out, not_4_out;

  not not_1 (not_1_out, q1);
  not not_2 (not_2_out, q0);
  not not_3 (not_3_out, q1);
  not not_4 (not_4_out, q0);
  and and_1 (ltop, not_1_out, not_2_out);
  not not_5 (bot, and_2_out);
  and and_2 (and_2_out, not_3_out, q0);
  not not_6 (lbot, q0);
  and and_3 (and_3_out, q1, not_4_out);
  not not_7 (rbot, and_3_out);

  assign out_6 = q1;
  assign rtop = 1'b1;
  assign top = bot;
endmodule

module mux (
  input  sel,
  input  New,
  input  Original,
  output out_4
);

  wire and_1_out, and_2_out, not_1_out;

  not not_1 (not_1_out, sel);
  and and_1 (and_1_out, sel, New);
  and and_2 (and_2_out, not_1_out, Original);
  or or_1 (out_4, and_1_out, and_2_out);
endmodule
